# Fritzing sketch desk-droid (saved by Fritzing 0.9.6b)
breadboards: 1
perfboards: 2

parts:
  A1 = ESP32-S3 supermini
  OLED_I2C1 = OLED 128x64 I2C Monochrome Display
  SG1 = Buzzer 12mm [part_number=COM-07950 package=buzzer-12mm-ns]
  Sensor1 = TTP223B Capacitive Touch Sensor Module
  TEMT6000_Breakout_Board1 = TEMT6000 Breakout Board [part_number=TEMT6000]
  M1 = DC Mini Metal Gear Motor
  M2 = DC Mini Metal Gear Motor
  R1 = Resistor [tolerance=±5% resistance=10k package="0603 [SMD]"]
  R2 = Resistor [tolerance=±5% resistance=10k package="0603 [SMD]"]
  U3 = LIPO-1000mAh [package=lipo-1000]
  U4 = L9110S H-bridge module - modified [part_number="L9110 H-bridge"]
  Part1 = Adafruit ADXL345 [part_number="Adafruit #1231"]
  OLED_I2C2 = OLED 128x64 I2C Monochrome Display
  Sensor2 = TTP223B Capacitive Touch Sensor Module
  TEMT6000_Breakout_Board2 = TEMT6000 Breakout Board [part_number=TEMT6000]
  M6 = DC Mini Metal Gear Motor
  M7 = DC Mini Metal Gear Motor
  J3 = Camdenboss CTB0158-4 [part_number=CTB0158-4 package=THT]
  A3 = ESP32-S3 supermini
  Part3 = Adafruit ADXL345 [part_number="Adafruit #1231"]
  U7 = L9110S H-bridge module - modified [part_number="L9110 H-bridge"]
  SG2 = Buzzer 12mm [part_number=COM-07950 package=buzzer-12mm-ns]
  J5 = Camdenboss CTB0158-2 [part_number=CTB0158-2 package=THT]
  U8 = LIPO-1000mAh [package=lipo-1000]
  J6 = Camdenboss CTB0158-4 [part_number=CTB0158-4 package=THT]
  R3 = Resistor [tolerance=±5% resistance=10k package="0603 [SMD]"]  # not connected
  R4 = Resistor [tolerance=±5% resistance=10k package="0603 [SMD]"]
  R5 = Resistor [tolerance=±5% resistance=10k package="0603 [SMD]"]  # not connected
  R6 = Resistor [tolerance=±5% resistance=10k package="0603 [SMD]"]  # not connected
  R7 = Resistor [tolerance=±5% resistance=10k package="0603 [SMD]"]
  R8 = Resistor [tolerance=±5% resistance=10k package="0603 [SMD]"]
  U9 = Header 2 [package=molex-1x2_lock]
  U10 = Header 2 [package=molex-1x2_lock]
  JP1 = Header 4 [package=screwterminal-3.5mm-4_lock]
  JP2 = Header 4 [package=screwterminal-3.5mm-4_lock]
  JP4 = Header 2 [package=jst-2-smd]

nets:
  GND: A1.Pin_1, A1.Pin_39, OLED_I2C1.GND, SG1.2, Sensor1.GND, TEMT6000_Breakout_Board1.GND, R2.Pin_0, U3.-, U4.IB2, Part1.GND, R7.Pin_0
  N1: A1.Pin_2, R1.Pin_1, U3.+
  N2: A1.Pin_5, R1.Pin_0, R2.Pin_1
  N3: A1.Pin_6, U4.IA1
  N4: A1.Pin_7, U4.IB1
  N5: A1.Pin_8, U4.GND, R7.Pin_1
  N6: A1.Pin_9, U4.VCC
  N7: A1.Pin_10, Part1.SDA/SDIO
  N8: A1.Pin_11, Part1.SCL
  N9: A1.Pin_32, TEMT6000_Breakout_Board1.SIG
  N10: A1.Pin_34, Sensor1.SIG
  N11: A1.Pin_35, SG1.1
  N12: A1.Pin_36, OLED_I2C1.SDA
  N13: A1.Pin_37, OLED_I2C1.SCK
  VCC: A1.Pin_38, OLED_I2C1.VDD, Sensor1.VCC, TEMT6000_Breakout_Board1.VCC, Part1.VCC
  N14: A1.Pin_40, U4.IA2
  N15: M1.IN1, U4.MOTOR_0B2
  N16: M1.IN2, U4.MOTOR_0A2
  N17: M2.IN1, U4.MOTOR_0B1
  N18: M2.IN2, U4.MOTOR_0A1
  N19: OLED_I2C2.SDA, J6.terminal_4
  N20: OLED_I2C2.SCK, J6.terminal_3
  N21: OLED_I2C2.VDD, J6.terminal_1
  N22: OLED_I2C2.GND, J6.terminal_2
  N23: Sensor2.SIG, A3.Pin_34
  N24: TEMT6000_Breakout_Board2.SIG, A3.Pin_32
  N25: M6.IN1, U7.MOTOR_0B2
  N26: M6.IN2, U7.MOTOR_0A2
  N27: M7.IN1, U7.MOTOR_0B1
  N28: M7.IN2, U7.MOTOR_0A1
  N29: J3.pin1, A3.Pin_9
  N30: J3.pin2, A3.Pin_8
  N31: J3.pin3, A3.Pin_7
  N32: J3.pin4, A3.Pin_6
  N33: J3.terminal_1, JP2.4
  N34: J3.terminal_2, JP2.3
  N35: J3.terminal_3, JP2.2
  N36: J3.terminal_4, JP2.1
  N37: A3.Pin_10, Part3.SDA/SDIO
  N38: A3.Pin_11, Part3.SCL
  N39: A3.Pin_35, SG2.1
  N40: A3.Pin_36, J6.pin4
  N41: A3.Pin_37, J6.pin3
  N42: A3.Pin_39, Part3.GND
  N43: A3.Pin_40, J5.pin1
  N44: U7.VCC, JP1.1
  N45: U7.GND, JP1.2
  N46: U7.IB1, R8.Pin_0, JP1.3
  N47: U7.IA1, JP1.4
  N48: U7.IB2, R8.Pin_1, U10.2
  N49: U7.IA2, U10.1
  N50: SG2.2, J5.pin2, J6.pin2
  N51: J5.terminal_1, U9.1
  N52: J5.terminal_2, U9.2
  N53: U8.-, JP4.1
  N54: R4.Pin_0, JP4.2

custom parts:
  ESP32-S3 supermini: Esp32-S3 Development board ESP32 SuperMini development board ESP32 Development board WiFi Bluetooth.
  Buzzer 12mm: Buzzer 12mm Spark Fun Electronics SKU : Comp-Buzzer Through hole This is a small 12mm round speaker that operates around the audible 2kHz range. You can use these speakers to create simple music or user interfaces. This is not a true piezoelectric speaker but behaves similarly. Instead of a piezoelectric crystal that vibrates with an electric current, this tiny speaker uses an electromagnet to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
  TTP223B Capacitive Touch Sensor Module: The TTP223B capacitive touch sensor module uses the TTP223B IC. The appropriate voltage is approximately 2 to 5.5 volts.
  TEMT6000 Breakout Board: The TEMT6000 is an ambient light sensor produced by Vishay Semiconductors. The sensor operates at both 3V3 and 5V and has analog output (with higher output voltage meaning more light) from the SIG pin.
  L9110S H-bridge module - modified: part-modified - L9110 H-bridge module
  Adafruit ADXL345: Filling out our accelerometer offerings, we now have the really lovely digital ADXL345 from Analog Devices, a triple-axis accelerometer with digital I2C and SPI interface breakout. We added an on-board 3.3V regulator and logic-level shifting circuitry, making it a perfect choice for interfacing with any 3V or 5V microcontroller such as the Arduino. The sensor has three axes of measurements, X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
